# Fritzing sketch PP2PS2 (saved by Fritzing 0.9.3b)
breadboards: 1

parts:
  パーツ1 = Arduino Nano (Rev3.0)
  IC1 = IC, DIP package, 14 pins [chip_label=74HC125]
  J1 = shrouded pin header, 16 pins [form="♂ (shrouded male)"]
  J2 = Camdenboss CTB0158-9 [part_number=CTB0158-9 package=THT]

nets:
  N1: パーツ1.GND, IC1.pin2, IC1.pin5, IC1.pin7, J1.pin4, J2.pin4
  N2: パーツ1.D2, J1.pin2
  N3: パーツ1.D3, J1.pin7
  N4: パーツ1.D4, J1.pin3
  N5: パーツ1.D9, IC1.pin1
  N6: パーツ1.D10, J2.pin6
  N7: パーツ1.D11/MOSI, J2.pin2
  N8: パーツ1.D12/MISO, IC1.pin4
  N9: パーツ1.D13/SCK, J2.pin7
  N10: IC1.pin3, J2.pin9
  N11: IC1.pin6, J2.pin1
  N12: IC1.pin9, IC1.pin10, IC1.pin12, IC1.pin13
  N13: J1.pin1, J2.pin5
